// Logisim project ALU.circ as structural Verilog
module main (
  input  [3:0] in_1,
  input  [3:0] in_2,
  input  in_3,
  input  in_4
);

  wire alu_1_aequalb, alu_1_agreaterb, alu_1_alessb;
  wire [3:0] alu_1_sum;

  ALU alu_1 (
    .A(in_1), .B(in_2), .S1(in_3), .So(in_4), .Sum(alu_1_sum), .AgreaterB(alu_1_agreaterb),
    .AequalB(alu_1_aequalb), .AlessB(alu_1_alessb));
  Hex_Digit_Display hex_digit_display_1 (.value(alu_1_sum));  // open: dp
  _7_Segment_Display u_7_segment_display_1 (
    .g(alu_1_aequalb), .a(alu_1_agreaterb), .d(alu_1_alessb));  // open: f, b, e, c, dp
endmodule

module OneBitFullAdder (
  input  A,
  input  B,
  input  Ci,
  output S,
  output Co
);

  wire and_1_out, and_2_out, xor_1_out;

  xor xor_1 (xor_1_out, A, B);
  and and_1 (and_1_out, xor_1_out, Ci);
  and and_2 (and_2_out, A, B);
  xor xor_2 (S, xor_1_out, Ci);
  or or_1 (Co, and_1_out, and_2_out);
endmodule

module FourBitAdder (
  input  [3:0] A,
  input  [3:0] B,
  input  S0,
  output [3:0] Sum
);

  wire onebitfulladder_1_co, onebitfulladder_2_co, onebitfulladder_3_co, xor_1_out, xor_2_out, xor_3_out,
       xor_4_out;

  xor xor_1 (xor_1_out, B[0], S0);
  xor xor_2 (xor_2_out, B[1], S0);
  xor xor_3 (xor_3_out, B[2], S0);
  xor xor_4 (xor_4_out, B[3], S0);
  OneBitFullAdder onebitfulladder_1 (.A(A[0]), .B(xor_1_out), .Ci(S0), .S(Sum[0]), .Co(onebitfulladder_1_co));
  OneBitFullAdder onebitfulladder_2 (
    .A(A[1]), .B(xor_2_out), .Ci(onebitfulladder_1_co), .S(Sum[1]), .Co(onebitfulladder_2_co));
  OneBitFullAdder onebitfulladder_3 (
    .A(A[2]), .B(xor_3_out), .Ci(onebitfulladder_2_co), .S(Sum[2]), .Co(onebitfulladder_3_co));
  OneBitFullAdder onebitfulladder_4 (.A(A[3]), .B(xor_4_out), .Ci(onebitfulladder_3_co), .S(Sum[3]));  // open: Co
  Hex_Digit_Display hex_digit_display_1 (.value(Sum));  // open: dp
endmodule

module Magnitude_Comparator (
  input  [3:0] A,
  input  [3:0] B,
  output AgreaterB,
  output AequalB,
  output AlessB
);

  wire and_1_out, and_2_out, and_3_out, and_4_out, and_5_out, and_6_out, and_7_out, and_8_out, not_1_out,
       not_2_out, not_3_out, not_4_out, not_5_out, not_6_out, not_7_out, not_8_out, xnor_1_out, xnor_2_out,
       xnor_3_out, xnor_4_out;

  not not_1 (not_1_out, B[0]);
  not not_2 (not_2_out, B[1]);
  not not_3 (not_3_out, B[2]);
  not not_4 (not_4_out, B[3]);
  xnor xnor_1 (xnor_1_out, A[0], B[0]);
  xnor xnor_2 (xnor_2_out, A[1], B[1]);
  xnor xnor_3 (xnor_3_out, A[2], B[2]);
  xnor xnor_4 (xnor_4_out, A[3], B[3]);
  not not_5 (not_5_out, A[3]);
  not not_6 (not_6_out, A[2]);
  not not_7 (not_7_out, A[1]);
  not not_8 (not_8_out, A[0]);
  and and_1 (and_1_out, A[0], not_1_out, xnor_2_out, xnor_3_out, xnor_4_out);
  and and_2 (and_2_out, A[1], not_2_out, xnor_3_out, xnor_4_out);
  and and_3 (and_3_out, A[2], not_3_out, xnor_4_out);
  and and_4 (and_4_out, A[3], not_4_out);
  and and_5 (and_5_out, B[3], not_5_out);
  and and_6 (and_6_out, xnor_4_out, B[2], not_6_out);
  and and_7 (and_7_out, xnor_4_out, xnor_3_out, B[1], not_7_out);
  and and_8 (and_8_out, xnor_4_out, xnor_3_out, xnor_2_out, B[0], not_8_out);
  or or_1 (AgreaterB, and_1_out, and_2_out, and_3_out, and_4_out);
  and and_9 (AequalB, xnor_1_out, xnor_2_out, xnor_3_out, xnor_4_out);
  or or_2 (AlessB, and_5_out, and_6_out, and_7_out, and_8_out);
endmodule

module A_equal_B (
  input  [3:0] A,
  input  AequalB,
  input  [3:0] B
);

  wire and_1_out, and_2_out, xnor_1_out, xnor_2_out, xnor_3_out, xnor_4_out;

  xnor xnor_1 (xnor_1_out, A[0], B[0]);
  xnor xnor_2 (xnor_2_out, A[1], B[1]);
  xnor xnor_3 (xnor_3_out, A[2], B[2]);
  xnor xnor_4 (xnor_4_out, A[3], B[3]);
  and and_1 (and_1_out, xnor_1_out, xnor_2_out);
  and and_2 (and_2_out, xnor_3_out, xnor_4_out);
  and and_3 (AequalB, and_1_out, and_2_out);
endmodule

module A_greater_B (
  input  [3:0] A,
  input  [3:0] B,
  output AgreaterB
);

  wire and_1_out, and_2_out, and_3_out, and_4_out, and_5_out, and_6_out, and_7_out, and_8_out, and_9_out,
       not_1_out, not_2_out, not_3_out, not_4_out, or_1_out, or_2_out, xnor_1_out, xnor_2_out, xnor_3_out;

  not not_1 (not_1_out, B[0]);
  not not_2 (not_2_out, B[1]);
  not not_3 (not_3_out, B[2]);
  not not_4 (not_4_out, B[3]);
  and and_1 (and_1_out, A[0], not_1_out);
  and and_2 (and_2_out, A[1], not_2_out);
  xnor xnor_1 (xnor_1_out, A[1], B[1]);
  xnor xnor_2 (xnor_2_out, A[2], B[2]);
  xnor xnor_3 (xnor_3_out, A[3], B[3]);
  and and_3 (and_3_out, A[2], not_3_out);
  and and_4 (and_4_out, A[3], not_4_out);
  and and_5 (and_5_out, xnor_2_out, xnor_3_out);
  and and_6 (and_6_out, xnor_3_out, and_3_out);
  and and_7 (and_7_out, xnor_1_out, and_5_out);
  and and_8 (and_8_out, and_1_out, and_7_out);
  and and_9 (and_9_out, and_2_out, and_5_out);
  or or_1 (or_1_out, and_8_out, and_9_out);
  or or_2 (or_2_out, and_6_out, and_4_out);
  or or_3 (AgreaterB, or_1_out, or_2_out);
endmodule

module Adder_Subtractor (
  input  [3:0] A,
  input  [3:0] B,
  input  S0,
  output [3:0] Sum
);

  wire onebitfulladder_1_co, onebitfulladder_2_co, onebitfulladder_3_co, xor_1_out, xor_2_out, xor_3_out,
       xor_4_out;

  xor xor_1 (xor_1_out, B[0], S0);
  xor xor_2 (xor_2_out, B[1], S0);
  xor xor_3 (xor_3_out, B[2], S0);
  xor xor_4 (xor_4_out, B[3], S0);
  OneBitFullAdder onebitfulladder_1 (.A(A[0]), .B(xor_1_out), .Ci(S0), .S(Sum[0]), .Co(onebitfulladder_1_co));
  OneBitFullAdder onebitfulladder_2 (
    .A(A[1]), .B(xor_2_out), .Ci(onebitfulladder_1_co), .S(Sum[1]), .Co(onebitfulladder_2_co));
  OneBitFullAdder onebitfulladder_3 (
    .A(A[2]), .B(xor_3_out), .Ci(onebitfulladder_2_co), .S(Sum[2]), .Co(onebitfulladder_3_co));
  OneBitFullAdder onebitfulladder_4 (.A(A[3]), .B(xor_4_out), .Ci(onebitfulladder_3_co), .S(Sum[3]));  // open: Co
endmodule

module ALU (
  input  [3:0] A,
  input  [3:0] B,
  input  S1,
  input  So,
  output [3:0] Sum,
  output AgreaterB,
  output AequalB,
  output AlessB
);

  wire [3:0] demultiplexer_1_out0, demultiplexer_1_out1, demultiplexer_2_out0, demultiplexer_2_out1;

  Demultiplexer #(.width(4)) demultiplexer_1 (
    .out0(demultiplexer_1_out0), .out1(demultiplexer_1_out1), .in(A), .sel(S1));
  Demultiplexer #(.width(4)) demultiplexer_2 (
    .out0(demultiplexer_2_out0), .out1(demultiplexer_2_out1), .in(B), .sel(S1));
  Adder_Subtractor adder_subtractor_1 (.A(demultiplexer_1_out0), .B(demultiplexer_2_out0), .S0(So), .Sum(Sum));
  Magnitude_Comparator magnitude_comparator_1 (
    .A(demultiplexer_1_out1), .B(demultiplexer_2_out1), .AgreaterB(AgreaterB), .AequalB(AequalB),
    .AlessB(AlessB));
endmodule
